// Logisim project ControladorDeSemáforos.circ as structural Verilog: 1 circuit, main circuit main
module main (
  input  siempre_en_1,
  input  [7:0] in_2,
  output [5:0] out_3
);

  wire and_1_out, and_2_out, and_3_out, and_4_out, and_5_out, clock_1_out, clock_2_out, comparator_1_eq,
       comparator_2_eq, comparator_3_eq, comparator_4_eq, comparator_5_eq, comparator_6_eq, d_ff_1_qn,
       d_ff_2_qn, decoder_1_out0, decoder_1_out1, decoder_1_out2, decoder_1_out3, decoder_1_out4,
       decoder_1_out5, decoder_1_out6, decoder_1_out7, decoder_1_out8, decoder_1_out9, decoder_1_out10,
       decoder_1_out11, decoder_1_out12, decoder_1_out13, decoder_1_out14, decoder_1_out15, decoder_2_out1,
       decoder_2_out2, decoder_2_out3, decoder_3_out1, decoder_3_out2, decoder_3_out3, decoder_4_out1,
       decoder_4_out2, decoder_4_out3, decoder_5_out1, decoder_5_out2, decoder_5_out3, decoder_6_out1,
       decoder_6_out2, decoder_6_out3, decoder_7_out1, decoder_7_out2, decoder_7_out3, decoder_8_out1,
       decoder_8_out2, decoder_8_out3, decoder_9_out1, decoder_9_out2, decoder_9_out3, decoder_10_out1,
       decoder_10_out2, decoder_10_out3, decoder_11_out1, decoder_11_out2, decoder_11_out3, decoder_12_out1,
       decoder_12_out2, decoder_12_out3, decoder_13_out1, decoder_13_out2, decoder_13_out3, decoder_14_out1,
       decoder_14_out2, decoder_14_out3, decoder_15_out1, decoder_15_out2, decoder_15_out3, decoder_16_out1,
       decoder_16_out2, decoder_16_out3, decoder_17_out1, decoder_17_out2, decoder_17_out3, not_1_out,
       not_2_out, not_3_out;
  wire [0:0] comparator_1_gt;
  wire [1:0] demultiplexer_1_out0, demultiplexer_1_out1, demultiplexer_1_out2, demultiplexer_1_out3,
       demultiplexer_1_out4, demultiplexer_1_out5, demultiplexer_1_out6, demultiplexer_1_out7,
       demultiplexer_1_out8, demultiplexer_1_out9, demultiplexer_1_out10, demultiplexer_1_out11,
       demultiplexer_1_out12, demultiplexer_1_out13, demultiplexer_1_out14, demultiplexer_1_out15,
       register_4_q, register_5_q, register_6_q, register_7_q, register_8_q, register_9_q, register_10_q,
       register_11_q, register_12_q, register_13_q, register_14_q, register_15_q, register_16_q,
       register_17_q, register_18_q, register_19_q;
  wire [3:0] diagrama_de_tiempos_data, diagrama_de_tiempos_data_2, diagrama_de_tiempos_data_3;
  wire [7:0] adder_1_out, adder_3_out, counter_1_q, counter_2_q, MAX_time_q, multiplexer_1_out, register_1_q,
       register_2_q, register_20_q;
  wire [11:0] adder_2_out, register_3_q;

  Clock clock_1 (.out(clock_1_out));
  Register #(.Select("low")) register_1 (
    .D({4'b0000, diagrama_de_tiempos_data_3}), .en(and_3_out), .Q(register_1_q), .clk(clock_1_out),
    .clr(and_1_out));
  Register #(.Select("low")) register_2 (
    .D(adder_1_out), .Q(register_2_q), .clk(clock_1_out), .clr(and_1_out));  // open: en
  D_Flip_Flop d_ff_1 (.clk(clock_1_out), .D(comparator_1_eq), .Qn(d_ff_1_qn));  // open: Q, preset, reset
  Comparator comparator_1 (
    .a(register_1_q), .b(register_2_q), .gt(comparator_1_gt[0]), .eq(comparator_1_eq));  // open: lt
  and and_1 (and_1_out, d_ff_1_qn, comparator_1_eq);
  Adder adder_1 (.a({{7{1'b0}}, comparator_1_gt[0]}), .b(register_2_q), .out(adder_1_out));  // open: cin, cout
  Adder #(.width(12)) adder_2 (
    .a(register_3_q), .b({{11{1'b0}}, comparator_1_gt[0]}), .out(adder_2_out));  // open: cin, cout
  Register #(.width(12), .Select("low")) register_3 (
    .D(adder_2_out), .Q(register_3_q), .clk(clock_1_out), .clr(and_5_out));  // open: en
  ROM #(.addrWidth(12), .dataWidth(6), .Select("low")) rom_1 (.addr(register_3_q), .data(out_3));
  Demultiplexer #(.select(4), .width(2), .enable("false")) demultiplexer_1 (
    .out0(demultiplexer_1_out0), .out1(demultiplexer_1_out1), .out2(demultiplexer_1_out2),
    .out3(demultiplexer_1_out3), .out4(demultiplexer_1_out4), .out5(demultiplexer_1_out5),
    .out6(demultiplexer_1_out6), .out7(demultiplexer_1_out7), .out8(demultiplexer_1_out8),
    .out9(demultiplexer_1_out9), .out10(demultiplexer_1_out10), .out11(demultiplexer_1_out11),
    .out12(demultiplexer_1_out12), .out13(demultiplexer_1_out13), .out14(demultiplexer_1_out14),
    .out15(demultiplexer_1_out15), .in(out_3[5:4]), .sel(out_3[3:0]));
  Decoder #(.select(4), .enable("false")) decoder_1 (
    .out0(decoder_1_out0), .out1(decoder_1_out1), .out2(decoder_1_out2), .out3(decoder_1_out3),
    .out4(decoder_1_out4), .out5(decoder_1_out5), .out6(decoder_1_out6), .out7(decoder_1_out7),
    .out8(decoder_1_out8), .out9(decoder_1_out9), .out10(decoder_1_out10), .out11(decoder_1_out11),
    .out12(decoder_1_out12), .out13(decoder_1_out13), .out14(decoder_1_out14), .out15(decoder_1_out15),
    .sel(out_3[3:0]));
  Comparator #(.width(12)) comparator_2 (.a({12{1'b0}}), .b(register_3_q), .eq(comparator_2_eq));  // open: gt, lt
  not not_1 (not_1_out, comparator_2_eq);
  and and_2 (and_2_out, not_1_out, decoder_1_out0);
  Register #(.width(2), .Select("low")) register_4 (
    .D(demultiplexer_1_out0), .en(and_2_out), .Q(register_4_q), .clk(clock_1_out));  // open: clr
  Register #(.width(2), .Select("low")) register_5 (
    .D(demultiplexer_1_out1), .en(decoder_1_out1), .Q(register_5_q), .clk(clock_1_out));  // open: clr
  Register #(.width(2), .Select("low")) register_6 (
    .D(demultiplexer_1_out2), .en(decoder_1_out2), .Q(register_6_q), .clk(clock_1_out));  // open: clr
  Register #(.width(2), .Select("low")) register_7 (
    .D(demultiplexer_1_out3), .en(decoder_1_out3), .Q(register_7_q), .clk(clock_1_out));  // open: clr
  Register #(.width(2), .Select("low")) register_8 (
    .D(demultiplexer_1_out4), .en(decoder_1_out4), .Q(register_8_q), .clk(clock_1_out));  // open: clr
  Register #(.width(2), .Select("low")) register_9 (
    .D(demultiplexer_1_out5), .en(decoder_1_out5), .Q(register_9_q), .clk(clock_1_out));  // open: clr
  Register #(.width(2), .Select("low")) register_10 (
    .D(demultiplexer_1_out6), .en(decoder_1_out6), .Q(register_10_q), .clk(clock_1_out));  // open: clr
  Register #(.width(2), .Select("low")) register_11 (
    .D(demultiplexer_1_out7), .en(decoder_1_out7), .Q(register_11_q), .clk(clock_1_out));  // open: clr
  Register #(.width(2), .Select("low")) register_12 (
    .D(demultiplexer_1_out8), .en(decoder_1_out8), .Q(register_12_q), .clk(clock_1_out));  // open: clr
  Register #(.width(2), .Select("low")) register_13 (
    .D(demultiplexer_1_out9), .en(decoder_1_out9), .Q(register_13_q), .clk(clock_1_out));  // open: clr
  Register #(.width(2), .Select("low")) register_14 (
    .D(demultiplexer_1_out10), .en(decoder_1_out10), .Q(register_14_q), .clk(clock_1_out));  // open: clr
  Register #(.width(2), .Select("low")) register_15 (
    .D(demultiplexer_1_out11), .en(decoder_1_out11), .Q(register_15_q), .clk(clock_1_out));  // open: clr
  Register #(.width(2), .Select("low")) register_16 (
    .D(demultiplexer_1_out12), .en(decoder_1_out12), .Q(register_16_q), .clk(clock_1_out));  // open: clr
  Register #(.width(2), .Select("low")) register_17 (
    .D(demultiplexer_1_out13), .en(decoder_1_out13), .Q(register_17_q), .clk(clock_1_out));  // open: clr
  Register #(.width(2), .Select("low")) register_18 (
    .D(demultiplexer_1_out14), .en(decoder_1_out14), .Q(register_18_q), .clk(clock_1_out));  // open: clr
  Register #(.width(2), .Select("low")) register_19 (
    .D(demultiplexer_1_out15), .en(decoder_1_out15), .Q(register_19_q), .clk(clock_1_out));  // open: clr
  not not_2 (not_2_out, comparator_5_eq);
  and and_3 (and_3_out, not_2_out, and_4_out);
  Clock #(.highDuration(2), .lowDuration(126)) clock_2 (.out(clock_2_out));
  and and_4 (and_4_out, clock_2_out, comparator_3_eq);
  not not_3 (not_3_out, siempre_en_1);
  Decoder #(.select(2), .enable("false")) decoder_2 (
    .out1(decoder_2_out1), .out2(decoder_2_out2), .out3(decoder_2_out3), .sel(register_4_q));  // open: out0
  Decoder #(.select(2), .enable("false")) decoder_3 (
    .out1(decoder_3_out1), .out2(decoder_3_out2), .out3(decoder_3_out3), .sel(register_5_q));  // open: out0
  Decoder #(.select(2), .enable("false")) decoder_4 (
    .out1(decoder_4_out1), .out2(decoder_4_out2), .out3(decoder_4_out3), .sel(register_6_q));  // open: out0
  Decoder #(.select(2), .enable("false")) decoder_5 (
    .out1(decoder_5_out1), .out2(decoder_5_out2), .out3(decoder_5_out3), .sel(register_7_q));  // open: out0
  Decoder #(.select(2), .enable("false")) decoder_6 (
    .out1(decoder_6_out1), .out2(decoder_6_out2), .out3(decoder_6_out3), .sel(register_8_q));  // open: out0
  Decoder #(.select(2), .enable("false")) decoder_7 (
    .out1(decoder_7_out1), .out2(decoder_7_out2), .out3(decoder_7_out3), .sel(register_9_q));  // open: out0
  Decoder #(.select(2), .enable("false")) decoder_8 (
    .out1(decoder_8_out1), .out2(decoder_8_out2), .out3(decoder_8_out3), .sel(register_10_q));  // open: out0
  Decoder #(.select(2), .enable("false")) decoder_9 (
    .out1(decoder_9_out1), .out2(decoder_9_out2), .out3(decoder_9_out3), .sel(register_11_q));  // open: out0
  Decoder #(.select(2), .enable("false")) decoder_10 (
    .out1(decoder_10_out1), .out2(decoder_10_out2), .out3(decoder_10_out3), .sel(register_12_q));  // open: out0
  Decoder #(.select(2), .enable("false")) decoder_11 (
    .out1(decoder_11_out1), .out2(decoder_11_out2), .out3(decoder_11_out3), .sel(register_13_q));  // open: out0
  Decoder #(.select(2), .enable("false")) decoder_12 (
    .out1(decoder_12_out1), .out2(decoder_12_out2), .out3(decoder_12_out3), .sel(register_14_q));  // open: out0
  Decoder #(.select(2), .enable("false")) decoder_13 (
    .out1(decoder_13_out1), .out2(decoder_13_out2), .out3(decoder_13_out3), .sel(register_15_q));  // open: out0
  Decoder #(.select(2), .enable("false")) decoder_14 (
    .out1(decoder_14_out1), .out2(decoder_14_out2), .out3(decoder_14_out3), .sel(register_16_q));  // open: out0
  Decoder #(.select(2), .enable("false")) decoder_15 (
    .out1(decoder_15_out1), .out2(decoder_15_out2), .out3(decoder_15_out3), .sel(register_17_q));  // open: out0
  Decoder #(.select(2), .enable("false")) decoder_16 (
    .out1(decoder_16_out1), .out2(decoder_16_out2), .out3(decoder_16_out3), .sel(register_18_q));  // open: out0
  Decoder #(.select(2), .enable("false")) decoder_17 (
    .out1(decoder_17_out1), .out2(decoder_17_out2), .out3(decoder_17_out3), .sel(register_19_q));  // open: out0
  Counter counter_1 (.Q(counter_1_q), .clk(clock_2_out), .clr(and_5_out));  // open: load, D, count, carry, preset, down
  Register #(.Select("low")) register_20 (
    .D(multiplexer_1_out), .en(not_3_out), .Q(register_20_q), .clk(clock_2_out), .clr(and_5_out));
  Adder adder_3 (.a(counter_2_q), .b(in_2), .out(adder_3_out));  // open: cin, cout
  LED led_1 (.in(decoder_2_out1));
  LED led_2 (.in(decoder_2_out2));
  LED led_3 (.in(decoder_2_out3));
  LED led_4 (.in(decoder_3_out1));
  LED led_5 (.in(decoder_3_out2));
  LED led_6 (.in(decoder_3_out3));
  LED led_7 (.in(decoder_4_out1));
  LED led_8 (.in(decoder_4_out2));
  LED led_9 (.in(decoder_4_out3));
  LED led_10 (.in(decoder_5_out1));
  LED led_11 (.in(decoder_5_out2));
  LED led_12 (.in(decoder_5_out3));
  LED led_13 (.in(decoder_6_out1));
  LED led_14 (.in(decoder_6_out2));
  LED led_15 (.in(decoder_6_out3));
  LED led_16 (.in(decoder_7_out1));
  LED led_17 (.in(decoder_7_out2));
  LED led_18 (.in(decoder_7_out3));
  LED led_19 (.in(decoder_8_out1));
  LED led_20 (.in(decoder_8_out2));
  LED led_21 (.in(decoder_8_out3));
  LED led_22 (.in(decoder_9_out1));
  LED led_23 (.in(decoder_9_out2));
  LED led_24 (.in(decoder_9_out3));
  LED led_25 (.in(decoder_10_out1));
  LED led_26 (.in(decoder_10_out2));
  LED led_27 (.in(decoder_10_out3));
  LED led_28 (.in(decoder_11_out1));
  LED led_29 (.in(decoder_11_out2));
  LED led_30 (.in(decoder_11_out3));
  LED led_31 (.in(decoder_12_out1));
  LED led_32 (.in(decoder_12_out2));
  LED led_33 (.in(decoder_12_out3));
  LED led_34 (.in(decoder_13_out1));
  LED led_35 (.in(decoder_13_out2));
  LED led_36 (.in(decoder_13_out3));
  LED led_37 (.in(decoder_14_out1));
  LED led_38 (.in(decoder_14_out2));
  LED led_39 (.in(decoder_14_out3));
  LED led_40 (.in(decoder_15_out1));
  LED led_41 (.in(decoder_15_out2));
  LED led_42 (.in(decoder_15_out3));
  LED led_43 (.in(decoder_16_out1));
  LED led_44 (.in(decoder_16_out2));
  LED led_45 (.in(decoder_16_out3));
  LED led_46 (.in(decoder_17_out1));
  LED led_47 (.in(decoder_17_out2));
  LED led_48 (.in(decoder_17_out3));
  Comparator comparator_3 (.a(counter_1_q), .b(register_20_q), .eq(comparator_3_eq));  // open: gt, lt
  Counter #(.ongoal("continue")) counter_2 (
    .D(adder_3_out), .Q(counter_2_q), .clk(comparator_3_eq), .clr(and_5_out));  // open: load, count, carry, preset, down
  Multiplexer #(.width(8), .enable("false")) multiplexer_1 (
    .in0({diagrama_de_tiempos_data_2, diagrama_de_tiempos_data}), .in1({4'b0000, diagrama_de_tiempos_data}),
    .out(multiplexer_1_out), .sel(comparator_4_eq));
  Comparator comparator_4 (.a(counter_2_q), .b({8{1'b0}}), .eq(comparator_4_eq));  // open: gt, lt
  Comparator comparator_5 (.a({8{1'b0}}), .b(counter_1_q), .eq(comparator_5_eq));  // open: gt, lt
  ROM #(.dataWidth(12), .Select("low")) diagrama_de_tiempos (
    .addr(counter_2_q),
    .data({diagrama_de_tiempos_data_3, diagrama_de_tiempos_data_2, diagrama_de_tiempos_data}));
  Register #(.Select("low")) MAX_time (
    .D({diagrama_de_tiempos_data_3, diagrama_de_tiempos_data_2}), .en(comparator_5_eq), .Q(MAX_time_q),
    .clk(clock_2_out));  // open: clr
  Comparator comparator_6 (.a(counter_1_q), .b(MAX_time_q), .eq(comparator_6_eq));  // open: gt, lt
  D_Flip_Flop d_ff_2 (.clk(clock_2_out), .D(comparator_6_eq), .Qn(d_ff_2_qn));  // open: Q, preset, reset
  and and_5 (and_5_out, d_ff_2_qn, comparator_6_eq);

  // Notes on the sheet:
  //   Semaforo
  //   Instrucción Estado-Semáforo
  //   contents of rom_1 (hex, n*v repeats v):
  //   0 30 31 12 13 20 21 10 11 32 33 22 23 12 13
  //   Estado
  //   Señal go go go, es decir,  ejecute este número de instrucciones rápidamente
  //   Comparador de contador con Diagrama de Tiempo
  //   Semáforo 1
  //   Semáforo 2
  //   Semáforo 3
  //   Semáforo 4
  //   Semáforo 5
  //   Semáforo 6
  //   Semáforo 7
  //   Semáforo 8
  //   Semáforo 9
  //   Semáforo 11
  //   Semáforo 12
  //   Semáforo 13
  //   Semáforo 14
  //   Semáforo 15
  //   Semáforo 16
  //   Cuando el contador se iguala al diagrama se suma uno
  //   Semáforo 10
  //   contents of diagrama_de_tiempos (hex, n*v repeats v):
  //   202 40c 20f 211 21b 21e 220 120
  //   Instrucciones: #Instructions, Tiempo, Tiempo
  //   #Instructions, viene siendo el número de semáforos que necesitan cambio
endmodule
